# Fritzing sketch 04-02-led (saved by Fritzing 0.9.3b)
breadboards: 1

parts:
  Raspberry_Pi_1 = Raspberry Pi 3 [part_number=RPI-3-V1.2]
  R1 = Resistor [tolerance=±5% resistance=220 package="2512 [SMD]"]
  LED1 = smd LED [color="Red (633nm)" package="1206 [SMD]"]

nets:
  N1: Raspberry_Pi_1.GPIO25, LED1.anode
  N2: Raspberry_Pi_1.GND, R1.Pin_0
  N3: R1.Pin_1, LED1.cathode

// code stored in the sketch: Untitled2.ino
import RPi.GPIO as GPIO
from time import sleep


PIN = 25
INTERVAL_SEC = 0.3


GPIO.setmode(GPIO.BCM)
GPIO.setup(PIN, GPIO.OUT)


try:
    while True:
        GPIO.output(PIN, not GPIO.input(PIN))
        sleep(INTERVAL_SEC)


except KeyboardInterrupt:
    pass
