# Fritzing sketch 05-03-sw-pd-event (saved by Fritzing 0.9.3b)
breadboards: 1

parts:
  S1 = Pushbutton [package="[THT]"]
  Raspberry_Pi_1 = Raspberry Pi 3 [part_number=RPI-3-V1.2]
  R2 = Resistor [tolerance=±5% resistance=220 package="0805 [SMD]"]
  LED1 = LED - 5mm [color="Red (633nm)" package="5 mm [THT]"]

nets:
  N1: S1.Pin_1, S1.Pin_2, Raspberry_Pi_1.GIPO24
  N2: S1.Pin_3, S1.Pin_4, Raspberry_Pi_1.3v3
  N3: Raspberry_Pi_1.GIPO25, R2.Pin_0
  N4: Raspberry_Pi_1.GND, LED1.anode

// code stored in the sketch: Untitled3.ino
mport RPi.GPIO as GPIO
from time import sleep

pin = 25
sw = 24
interval_sec = 0.05

def my_callback(channel):
    if channel != sw:
        return

    global stat
    stat = not stat
    GPIO.output(pin, stat)

GPIO.setmode(GPIO.BCM)
GPIO.setup(pin, GPIO.OUT, initial=GPIO.LOW)
GPIO.setup(sw, GPIO.IN, pull_up_down=GPIO.PUD_DOWN)
GPIO.add_event_detect(sw, GPIO.RISING, callback=my_callback, bouncetime=200)

stat = False
try:
    while True:
        sleep(interval_sec)

except KeyboardInterrupt:
    pass

GPIO.cleanup()
